// Logisim project ALU.circ as structural Verilog: 1 circuit, main circuit main
module main (
  input  A0,
  input  A1,
  input  A2,
  input  A3,
  input  CS2,
  input  CS1,
  input  CS0,
  input  B0,
  input  B1,
  input  B2,
  input  B3,
  output F0,
  output F1,
  output F2,
  output F3,
  output C,
  output Z,
  output S,
  output V
);

  wire main_1__6__s2, main_1_cout, main_2__6__s2, main_2_cout, n7404_1_p2, n7404_1_p4, n7404_1_p6,
       n7404_1_p9, n7404_1_p10, n7404_1_p11, n7404_1_p12, n7404_1_p13, n7404_1_p14, n7408_1_p2, n7408_1_p3,
       n7408_1_p6, n7408_1_p11, n7408_1_p14, n7408_2_p6, n7408_2_p10, n7408_2_p11, n7408_2_p14, n7408_3_p3,
       n7408_3_p12, n7432_1_p3, n7432_1_p6, n7432_1_p11, n7432_1_p14;

  // _7404 7404_1: pin names not known; wires that end beside it: CS2, n7404_1_p2, CS1, n7404_1_p4, CS0, n7404_1_p6, 1'b0, 1'b1, n7404_1_p9, n7404_1_p10, n7404_1_p11, n7404_1_p12, n7404_1_p13, n7404_1_p14
  // _7408 7408_1: pin names not known; wires that end beside it: B0, n7408_1_p2, n7408_1_p3, B1, n7408_1_p2, n7408_1_p6, 1'b0, 1'b1, B2, n7408_1_p2, n7408_1_p11, n7408_1_p2, B3, n7408_1_p14
  // _7408 7408_2: pin names not known; wires that end beside it: CS2, n7404_1_p4, n7404_1_p13, n7404_1_p6, n7404_1_p14, n7408_2_p6, 1'b0, 1'b1, n7404_1_p13, n7408_2_p10, n7408_2_p11, n7404_1_p2, CS0, n7408_2_p14
  // _7432 7432_1: pin names not known; wires that end beside it: n7408_2_p6, n7408_1_p3, n7432_1_p3, n7408_2_p6, n7408_1_p6, n7432_1_p6, 1'b0, 1'b1, n7408_2_p6, n7408_1_p11, n7432_1_p11, n7408_2_p6, n7408_1_p14, n7432_1_p14
  // _7432 7432_2: pin names not known; wires that end beside it: CS2, CS1, n7408_1_p2, n7408_2_p14, n7404_1_p4, n7408_2_p10, 1'b0, 1'b1, F0, F1, n7404_1_p9, F3, F2, n7404_1_p11
  adderseparate_main main_1 (
    ._1__A4(A1), ._3__A3(n7408_2_p10), ._4__B3(main_1__6__s2), ._5__Vcc(1'b1), ._6__S2(main_1__6__s2),
    ._7__B2(1'b0), ._8__A2(1'b0), ._16__B4(n7432_1_p6), ._15__S4(F1), .Cout(main_1_cout),
    ._13__Cin(n7408_2_p11), ._12__GND(1'b0), ._11__B1(n7432_1_p3), ._10__A1(A0), ._9__S1(F0));  // open: _2__S3
  adderseparate_main main_2 (
    ._1__A4(A3), ._3__A3(n7408_2_p10), ._4__B3(main_2__6__s2), ._5__Vcc(1'b1), ._6__S2(main_2__6__s2),
    ._7__B2(1'b0), ._8__A2(1'b0), ._16__B4(n7432_1_p14), ._15__S4(F3), .Cout(main_2_cout),
    ._13__Cin(n7408_3_p3), ._12__GND(1'b0), ._11__B1(n7432_1_p11), ._10__A1(A2), ._9__S1(F2));  // open: _2__S3
  // _7408 7408_3: pin names not known; wires that end beside it: main_1_cout, n7408_2_p10, n7408_3_p3, main_2_cout, n7408_2_p10, C, 1'b0, 1'b1, n7404_1_p10, n7404_1_p12, Z, n7408_3_p12, n7408_2_p10, V
  // _7486 7486_1: pin names not known; wires that end beside it: main_2_cout, main_2__6__s2, n7408_3_p12, 1'b0, 1'b1

  assign S = F3;

  // Notes on the sheet:
  //   A/L
  //   Cin
  //   Y0
  //   Y1
  //   Y2
  //   Y3
endmodule
